# Fritzing sketch sketch (saved by Fritzing 0.9.9b)
breadboards: 1

parts:
  A1 = TS-300B interface
  A2 = TS 300B sensor
  A3 = TS 300B sensor
  A4 = TS-300B interface
  M2 = PH meter with sensor in breadboard [package=THT]
  M3 = PH meter with sensor in breadboard [package=THT]
  DS1 = DS18B20 1-Wire Temperature Sensor Probe
  DS2 = DS18B20 1-Wire Temperature Sensor Probe
  A5 = tds-sensor-meter-v1.0_1
  A6 = tds-sensor-meter-v1.0_1
  part = LCD1602-I2C
  part_2 = Arduino Mega ADK (Rev3)

nets:
  VCC: A1.Pin_1, A1.Pin_8, A2.Pin_3, A3.Pin_3, A4.Pin_1, A4.Pin_8, M2.pin2, M3.pin2, part.VCC, part_2.IOREF, part_2.5V
  N1: A1.Pin_2, part_2.A9
  GND: A1.Pin_4, A4.Pin_4, M2.pin3, M3.pin3, DS1.GND, DS2.GND, A5.pin3, A6.pin3, part.GND, part_2.GND
  N2: A1.Pin_5, A2.Pin_1
  N3: A1.Pin_6, A2.Pin_2
  N4: A3.Pin_1, A4.Pin_5
  N5: A3.Pin_2, A4.Pin_6
  N6: A4.Pin_2, part_2.A8
  N7: M2.pin1, part_2.A7
  N8: M3.pin1, part_2.A6
  N9: DS1.DQ, part_2.A0
  VDD: DS1.VDD, DS2.VDD, A5.pin2, A6.pin2
  N10: DS2.DQ, part_2.A1
  N11: A5.pin1, part_2.A3
  N12: A6.pin1, part_2.A2
  N13: part.SDA, part_2.A5
  N14: part.SCL, part_2.A4

custom parts:
  TS-300B interface: TS-300B interface.
  TS 300B sensor: TS 300B water turbidity sensor.
  PH meter with sensor in breadboard: DFrobot PH meter (SKU SEN0161)
  : TDS Meter V1.0 Development Board Water Meter Filter Measuring Water Sensor Module.
  LCD1602-I2C: A standard character display, usually with 2x16 characters. Comes in many colors with LCM1602 IIC attached.
